# Fritzing sketch RC522_D1mini 2 (saved by Fritzing 0.9.3b)
circuit board: 6.5cm x 4.5cm
breadboards: 1

parts:
  MFRC522 = RFID-RC522-v2
  S1 = Momentary Switch 6mm 2pin
  TRM1 = Terminal 2pin
  TRM2 = Terminal 2pin
  LED1 = LED - 5mm [color="Red (633nm)" package="5 mm [THT]"]
  LED2 = LED - 5mm [color="Red (633nm)" package="5 mm [THT]"]
  WeMos_D1_Mini1 = WeMos D1 Mini

nets:
  N1: MFRC522.SDA, WeMos_D1_Mini1.D8
  N2: MFRC522.SCK, WeMos_D1_Mini1.D5
  N3: MFRC522.MOSI, WeMos_D1_Mini1.D7
  N4: MFRC522.MISO, WeMos_D1_Mini1.D6
  N5: MFRC522.GND, S1.2, TRM2.pin_1, LED1.cathode, LED2.cathode, WeMos_D1_Mini1.G
  N6: MFRC522.RST, WeMos_D1_Mini1.D0
  3.3V: MFRC522.3.3V, WeMos_D1_Mini1.3V3
  N7: S1.1, WeMos_D1_Mini1.D3
  N8: TRM1.pin_1, LED2.anode, WeMos_D1_Mini1.D2
  N9: TRM1.pin_2, LED1.anode, WeMos_D1_Mini1.D1
  N10: TRM2.pin_2, WeMos_D1_Mini1.5V

custom parts:
  RFID-RC522-v2: A simple China made RFID-RC522 Reader; do check the pin labels, as this is a MFRC522 based clone.
  Momentary Switch 6mm 2pin: Momentary Switch 6mm 2 pin Button commonly used for reset or general input.
  Terminal 2pin: 2-pin Terminal Block
  WeMos D1 Mini: The D1 mini is a mini wifi board based on ESP-8266EX.
